# Fritzing sketch PCA9685_example (saved by Fritzing 0.9.0b)
breadboards: 1

parts:
  IC1 = HT SSOP28 [chip_label=PCA9685 package=HTSSOP28]
  LED1 = LED - 5mm [color="Red (633nm)" package="5 mm [THT]"]
  R1 = Resistor [tolerance=±5% resistance=220 package=THT]
  LED2 = LED - 5mm [color="Red (633nm)" package="5 mm [THT]"]
  R2 = Resistor [tolerance=±5% resistance=220 package=THT]
  LED3 = LED - 5mm [color="Red (633nm)" package="5 mm [THT]"]
  LED4 = LED - 5mm [color="Red (633nm)" package="5 mm [THT]"]
  R3 = Resistor [tolerance=±5% resistance=220 package=THT]
  R4 = Resistor [tolerance=±5% resistance=220 package=THT]
  Bauteil1 = Arduino Uno (Rev3)

nets:
  GND: IC1.A0, IC1.A1, IC1.A2, IC1.A3, IC1.A4, IC1.VSS, IC1.OE, IC1.A5, IC1.EXTCLK, Bauteil1.GND
  N1: IC1.LED0, LED1.cathode
  N2: IC1.LED1, LED2.cathode
  N3: IC1.LED2, LED3.cathode
  N4: IC1.LED3, LED4.cathode
  N5: IC1.SCL, Bauteil1.A5/SCL
  N6: IC1.SCA, Bauteil1.A4/SDA
  VDD: IC1.VDD, R1.Pin_1, R2.Pin_1, R3.Pin_1, R4.Pin_1, Bauteil1.5V
  N7: LED1.anode, R1.Pin_0
  N8: LED2.anode, R2.Pin_0
  N9: LED3.anode, R3.Pin_0
  N10: LED4.anode, R4.Pin_0
